# Fritzing sketch Mechatronics-Challenge (saved by Fritzing 0.9.3b)
breadboards: 1

parts:
  Carloop_GPS_Photon_Shield_Connector = IC, DIP package, 24 pins [chip_label="Carloop GPS Photon Shield Connector"]
  Part1 = Photon
  5V_Power_Supply = Power plug

nets:
  N1: Carloop_GPS_Photon_Shield_Connector.pin1, Part1.3V3
  GND: Carloop_GPS_Photon_Shield_Connector.pin2, Part1.GND, 5V_Power_Supply.GND
  N2: Carloop_GPS_Photon_Shield_Connector.pin3, Part1.RX
  N3: Carloop_GPS_Photon_Shield_Connector.pin4, Part1.TX
  N4: Carloop_GPS_Photon_Shield_Connector.pin7, Part1.A5
  N5: Carloop_GPS_Photon_Shield_Connector.pin8, Part1.A4
  N6: Carloop_GPS_Photon_Shield_Connector.pin9, Part1.A3
  N7: Carloop_GPS_Photon_Shield_Connector.pin18, Part1.A2
  VIN: Part1.VIN, 5V_Power_Supply.VCC
